// Logisim project CPU.circ as structural Verilog: 29 circuits, main circuit full_adder
module encoder_4 (
  input  [3:0] I,
  output [1:0] Q
);

  or or_1 (Q[0], I[1], I[3]);
  or or_2 (Q[1], I[2], I[3]);
endmodule

module decoder_4 (
  input  [1:0] I,
  output [3:0] Q
);

  wire [1:0] not_1_out;

  assign not_1_out = ~I;  // NOT_Gate not_1, 2 bits wide
  and and_1 (Q[0], not_1_out[0], not_1_out[1]);
  and and_2 (Q[1], I[0], not_1_out[1]);
  and and_3 (Q[2], not_1_out[0], I[1]);
  and and_4 (Q[3], I[0], I[1]);
endmodule

module encoder_16 (
  input  [15:0] I,
  output [3:0] Q
);

  or or_1 (Q[0], I[1], I[3], I[5], I[7], I[9], I[11], I[13], I[15]);
  or or_2 (Q[1], I[2], I[3], I[6], I[7], I[10], I[11], I[14], I[15]);
  or or_3 (Q[2], I[4], I[5], I[6], I[7], I[12], I[13], I[14], I[15]);
  or or_4 (Q[3], I[8], I[9], I[10], I[11], I[12], I[13], I[14], I[15]);
endmodule

module decoder_16 (
  input  [3:0] I,
  output [15:0] Q
);

  wire [3:0] not_1_out;

  assign not_1_out = ~I;  // NOT_Gate not_1, 4 bits wide
  and and_1 (Q[0], not_1_out[0], not_1_out[1], not_1_out[2], not_1_out[3]);
  and and_2 (Q[1], I[0], not_1_out[1], not_1_out[2], not_1_out[3]);
  and and_3 (Q[2], not_1_out[0], I[1], not_1_out[2], not_1_out[3]);
  and and_4 (Q[3], I[0], I[1], not_1_out[2], not_1_out[3]);
  and and_5 (Q[4], not_1_out[0], not_1_out[1], I[2], not_1_out[3]);
  and and_6 (Q[5], I[0], not_1_out[1], I[2], not_1_out[3]);
  and and_7 (Q[6], not_1_out[0], I[1], I[2], not_1_out[3]);
  and and_8 (Q[7], I[0], I[1], I[2], not_1_out[3]);
  and and_9 (Q[8], not_1_out[0], not_1_out[1], not_1_out[2], I[3]);
  and and_10 (Q[9], I[0], not_1_out[1], not_1_out[2], I[3]);
  and and_11 (Q[10], not_1_out[0], I[1], not_1_out[2], I[3]);
  and and_12 (Q[11], I[0], I[1], not_1_out[2], I[3]);
  and and_13 (Q[12], not_1_out[0], not_1_out[1], I[2], I[3]);
  and and_14 (Q[13], I[0], not_1_out[1], I[2], I[3]);
  and and_15 (Q[14], not_1_out[0], I[1], I[2], I[3]);
  and and_16 (Q[15], I[0], I[1], I[2], I[3]);
endmodule

module multiplexer_2_4 (
  input  S,
  input  [3:0] A,
  input  [3:0] B,
  output [3:0] Q
);

  wire and_1_out, and_2_out, and_3_out, and_4_out, and_5_out, and_6_out, and_7_out, and_8_out, not_1_out;

  not not_1 (not_1_out, S);
  and and_1 (and_1_out, A[0], not_1_out);
  and and_2 (and_2_out, B[0], S);
  and and_3 (and_3_out, A[1], not_1_out);
  and and_4 (and_4_out, B[1], S);
  and and_5 (and_5_out, A[2], not_1_out);
  and and_6 (and_6_out, B[2], S);
  and and_7 (and_7_out, A[3], not_1_out);
  and and_8 (and_8_out, B[3], S);
  or or_1 (Q[0], and_1_out, and_2_out);
  or or_2 (Q[1], and_3_out, and_4_out);
  or or_3 (Q[2], and_5_out, and_6_out);
  or or_4 (Q[3], and_7_out, and_8_out);
endmodule

module demultiplexer_2_4 (
  input  S,
  input  [3:0] Q,
  output [3:0] A,
  output [3:0] B
);

  wire not_1_out;

  not not_1 (not_1_out, S);
  and and_1 (A[0], not_1_out, Q[0]);
  and and_2 (A[1], not_1_out, Q[1]);
  and and_3 (A[2], not_1_out, Q[2]);
  and and_4 (A[3], not_1_out, Q[3]);
  and and_5 (B[0], S, Q[0]);
  and and_6 (B[1], S, Q[1]);
  and and_7 (B[2], S, Q[2]);
  and and_8 (B[3], S, Q[3]);
endmodule

module mulitplexer_2_8 (
  input  S,
  input  [7:0] A,
  input  [7:0] B,
  output [7:0] Q
);

  wire and_1_out, and_2_out, and_3_out, and_4_out, and_5_out, and_6_out, and_7_out, and_8_out, and_9_out,
       and_10_out, and_11_out, and_12_out, and_13_out, and_14_out, and_15_out, and_16_out, not_1_out;

  not not_1 (not_1_out, S);
  and and_1 (and_1_out, A[0], not_1_out);
  and and_2 (and_2_out, B[0], S);
  and and_3 (and_3_out, A[1], not_1_out);
  and and_4 (and_4_out, B[1], S);
  and and_5 (and_5_out, A[2], not_1_out);
  and and_6 (and_6_out, B[2], S);
  and and_7 (and_7_out, A[3], not_1_out);
  and and_8 (and_8_out, B[3], S);
  and and_9 (and_9_out, A[4], not_1_out);
  and and_10 (and_10_out, B[4], S);
  and and_11 (and_11_out, A[5], not_1_out);
  and and_12 (and_12_out, B[5], S);
  and and_13 (and_13_out, A[6], not_1_out);
  and and_14 (and_14_out, B[6], S);
  and and_15 (and_15_out, A[7], not_1_out);
  and and_16 (and_16_out, B[7], S);
  or or_1 (Q[0], and_1_out, and_2_out);
  or or_2 (Q[1], and_3_out, and_4_out);
  or or_3 (Q[2], and_5_out, and_6_out);
  or or_4 (Q[3], and_7_out, and_8_out);
  or or_5 (Q[4], and_9_out, and_10_out);
  or or_6 (Q[5], and_11_out, and_12_out);
  or or_7 (Q[6], and_13_out, and_14_out);
  or or_8 (Q[7], and_15_out, and_16_out);
endmodule

module demultiplexer_2_8 (
  input  S,
  input  [7:0] Q,
  output [7:0] A,
  output [7:0] B
);

  wire not_1_out;

  not not_1 (not_1_out, S);
  and and_1 (A[0], not_1_out, Q[0]);
  and and_2 (A[1], not_1_out, Q[1]);
  and and_3 (A[2], not_1_out, Q[2]);
  and and_4 (A[3], not_1_out, Q[3]);
  and and_5 (A[4], not_1_out, Q[4]);
  and and_6 (A[5], not_1_out, Q[5]);
  and and_7 (A[6], not_1_out, Q[6]);
  and and_8 (A[7], not_1_out, Q[7]);
  and and_9 (B[0], S, Q[0]);
  and and_10 (B[1], S, Q[1]);
  and and_11 (B[2], S, Q[2]);
  and and_12 (B[3], S, Q[3]);
  and and_13 (B[4], S, Q[4]);
  and and_14 (B[5], S, Q[5]);
  and and_15 (B[6], S, Q[6]);
  and and_16 (B[7], S, Q[7]);
endmodule

module parity_detector_8 (
  input  [7:0] D,
  output P
);

  wire xor_1_out, xor_2_out, xor_3_out, xor_4_out, xor_5_out, xor_6_out;

  xor xor_1 (xor_1_out, D[0], D[1]);
  xor xor_2 (xor_2_out, D[2], D[3]);
  xor xor_3 (xor_3_out, D[4], D[5]);
  xor xor_4 (xor_4_out, D[6], D[7]);
  xor xor_5 (xor_5_out, xor_1_out, xor_2_out);
  xor xor_6 (xor_6_out, xor_3_out, xor_4_out);
  xor xor_7 (P, xor_5_out, xor_6_out);
endmodule

module controlled_invertor_8 (
  input  [7:0] D,
  input  I,
  output [7:0] Q
);

  xor xor_1 (Q[0], D[0], I);
  xor xor_2 (Q[1], D[1], I);
  xor xor_3 (Q[2], D[2], I);
  xor xor_4 (Q[3], D[3], I);
  xor xor_5 (Q[4], D[4], I);
  xor xor_6 (Q[5], D[5], I);
  xor xor_7 (Q[6], D[6], I);
  xor xor_8 (Q[7], D[7], I);
endmodule

module comparitor_8 (
  input  [7:0] A,
  input  [7:0] B,
  output EQ
);

  wire xor_1_out, xor_2_out, xor_3_out, xor_4_out, xor_5_out, xor_6_out, xor_7_out, xor_8_out;

  xor xor_1 (xor_1_out, A[0], B[0]);
  xor xor_2 (xor_2_out, A[1], B[1]);
  xor xor_3 (xor_3_out, A[2], B[2]);
  xor xor_4 (xor_4_out, A[3], B[3]);
  xor xor_5 (xor_5_out, A[4], B[4]);
  xor xor_6 (xor_6_out, A[5], B[5]);
  xor xor_7 (xor_7_out, A[6], B[6]);
  xor xor_8 (xor_8_out, A[7], B[7]);
  nor nor_1 (EQ, xor_1_out, xor_2_out, xor_3_out, xor_4_out, xor_5_out, xor_6_out, xor_7_out, xor_8_out);
endmodule

module enabler_8 (
  input  [7:0] D,
  input  E,
  output [7:0] Q
);

  and and_1 (Q[0], D[0], E);
  and and_2 (Q[1], D[1], E);
  and and_3 (Q[2], D[2], E);
  and and_4 (Q[3], D[3], E);
  and and_5 (Q[4], D[4], E);
  and and_6 (Q[5], D[5], E);
  and and_7 (Q[6], D[6], E);
  and and_8 (Q[7], D[7], E);
endmodule

module half_adder (
  input  A,
  input  B,
  output CO,
  output S
);

  and and_1 (CO, A, B);
  xor xor_1 (S, A, B);
endmodule

module full_adder (
  input  CI,
  input  A,
  input  B,
  output CO,
  output S
);

  wire and_1_out, and_2_out, and_3_out, xor_1_out;

  and and_1 (and_1_out, CI, A);
  and and_2 (and_2_out, CI, B);
  and and_3 (and_3_out, A, B);
  xor xor_1 (xor_1_out, CI, A);
  or or_1 (CO, and_1_out, and_2_out, and_3_out);
  xor xor_2 (S, xor_1_out, B);
endmodule

module ripple_adder_8 (
  input  CI,
  input  [7:0] A,
  input  [7:0] B,
  output [7:0] S,
  output CO
);

  wire full_adder_1_co, full_adder_2_co, full_adder_3_co, full_adder_4_co, full_adder_5_co, full_adder_6_co,
       full_adder_7_co;

  full_adder full_adder_1 (.CI(CI), .A(A[0]), .B(B[0]), .CO(full_adder_1_co), .S(S[0]));
  full_adder full_adder_2 (.CI(full_adder_1_co), .A(A[1]), .B(B[1]), .CO(full_adder_2_co), .S(S[1]));
  full_adder full_adder_3 (.CI(full_adder_2_co), .A(A[2]), .B(B[2]), .CO(full_adder_3_co), .S(S[2]));
  full_adder full_adder_4 (.CI(full_adder_3_co), .A(A[3]), .B(B[3]), .CO(full_adder_4_co), .S(S[3]));
  full_adder full_adder_5 (.CI(full_adder_4_co), .A(A[4]), .B(B[4]), .CO(full_adder_5_co), .S(S[4]));
  full_adder full_adder_6 (.CI(full_adder_5_co), .A(A[5]), .B(B[5]), .CO(full_adder_6_co), .S(S[5]));
  full_adder full_adder_7 (.CI(full_adder_6_co), .A(A[6]), .B(B[6]), .CO(full_adder_7_co), .S(S[6]));
  full_adder full_adder_8 (.CI(full_adder_7_co), .A(A[7]), .B(B[7]), .CO(CO), .S(S[7]));
endmodule

module arithmetic_unit_8 (
  input  CI,
  input  [7:0] A,
  input  [7:0] B,
  input  E,
  input  SU,
  output [7:0] S,
  output CO,
  output [7:0] I
);

  wire or_1_out;
  wire [7:0] controlled_invertor_8_1_q;

  or or_1 (or_1_out, CI, SU);
  ripple_adder_8 ripple_adder_8_1 (.CI(or_1_out), .A(A), .B(controlled_invertor_8_1_q), .S(I), .CO(CO));
  controlled_invertor_8 controlled_invertor_8_1 (.D(B), .I(SU), .Q(controlled_invertor_8_1_q));
  assign S = E ? I : 8'bz;  // Controlled_Buffer controlled_buffer_1
endmodule

module arithmetic_logic_unit_8 (
  input  [7:0] A,
  input  [7:0] B,
  input  E,
  input  SU,
  input  CI,
  input  [1:0] OP,
  output [7:0] I,
  output [7:0] Q,
  output CO
);

  wire [3:0] decoder_4_1_q;
  wire [7:0] and_1_out, arithmetic_unit_8_1_s, not_1_out, or_1_out;

  assign not_1_out = ~A;  // NOT_Gate not_1, 8 bits wide
  assign and_1_out = A & B;  // AND_Gate and_1, 8 bits wide
  assign or_1_out = A | B;  // OR_Gate or_1, 8 bits wide
  decoder_4 decoder_4_1 (.I(OP), .Q(decoder_4_1_q));
  arithmetic_unit_8 arithmetic_unit_8_1 (
    .CI(CI), .A(A), .B(B), .E(1'b1), .SU(SU), .S(arithmetic_unit_8_1_s), .CO(CO));  // open: I
  assign I = decoder_4_1_q[1] ? and_1_out : 8'bz;  // Controlled_Buffer controlled_buffer_1
  assign I = decoder_4_1_q[2] ? or_1_out : 8'bz;  // Controlled_Buffer controlled_buffer_2
  assign I = decoder_4_1_q[3] ? not_1_out : 8'bz;  // Controlled_Buffer controlled_buffer_3
  assign I = decoder_4_1_q[0] ? arithmetic_unit_8_1_s : 8'bz;  // Controlled_Buffer controlled_buffer_4
  assign Q = E ? I : 8'bz;  // Controlled_Buffer controlled_buffer_5
endmodule

module s_latch (
  input  S,
  output Q
);

  or or_1 (Q, S, Q);
endmodule

module sr_latch (
  input  R,
  input  S,
  output Q,
  output NQ
);

  nor nor_1 (Q, R, NQ);
  nor nor_2 (NQ, Q, S);
endmodule

module d_latch (
  input  D,
  input  E,
  input  RE,
  output Q,
  output NQ
);

  wire and_1_out, and_2_out, not_1_out, or_1_out;

  not not_1 (not_1_out, D);
  and and_1 (and_1_out, not_1_out, E);
  and and_2 (and_2_out, E, D);
  or or_1 (or_1_out, and_1_out, RE);
  sr_latch sr_latch_1 (.R(or_1_out), .S(and_2_out), .Q(Q), .NQ(NQ));
endmodule

module d_flip_flop (
  input  D,
  input  CLK,
  input  RE,
  output Q,
  output NQ
);

  D_Flip_Flop d_ff_1 (.D(D), .clk(CLK), .Q(Q), .Qn(NQ), .reset(RE));  // open: preset
endmodule

module data_register_1 (
  input  D,
  input  L,
  input  CLK,
  input  E,
  input  RE,
  output Q,
  output I
);

  wire and_1_out, and_2_out, not_1_out, or_1_out;

  not not_1 (not_1_out, L);
  and and_1 (and_1_out, I, not_1_out);
  and and_2 (and_2_out, D, L);
  or or_1 (or_1_out, and_1_out, and_2_out);
  d_flip_flop d_flip_flop_1 (.D(or_1_out), .CLK(CLK), .RE(RE), .Q(I));  // open: NQ
  assign Q = E ? I : 1'bz;  // Controlled_Buffer controlled_buffer_1
endmodule

module data_register_4 (
  input  [3:0] D,
  input  L,
  input  E,
  input  CLK,
  input  RE,
  output [3:0] Q,
  output [3:0] I
);

  data_register_1 data_register_1_1 (.D(D[0]), .L(L), .CLK(CLK), .E(1'b1), .RE(RE), .Q(I[0]));  // open: I
  data_register_1 data_register_1_2 (.D(D[1]), .L(L), .CLK(CLK), .E(1'b1), .RE(RE), .Q(I[1]));  // open: I
  data_register_1 data_register_1_3 (.D(D[2]), .L(L), .CLK(CLK), .E(1'b1), .RE(RE), .Q(I[2]));  // open: I
  data_register_1 data_register_1_4 (.D(D[3]), .L(L), .CLK(CLK), .E(1'b1), .RE(RE), .Q(I[3]));  // open: I
  assign Q = E ? I : 4'bz;  // Controlled_Buffer controlled_buffer_1
endmodule

module data_register_8 (
  input  [7:0] D,
  input  L,
  input  E,
  input  CLK,
  input  RE,
  output [7:0] Q,
  output [7:0] I
);

  data_register_1 data_register_1_1 (.D(D[0]), .L(L), .CLK(CLK), .E(1'b1), .RE(RE), .Q(I[0]));  // open: I
  data_register_1 data_register_1_2 (.D(D[1]), .L(L), .CLK(CLK), .E(1'b1), .RE(RE), .Q(I[1]));  // open: I
  data_register_1 data_register_1_3 (.D(D[2]), .L(L), .CLK(CLK), .E(1'b1), .RE(RE), .Q(I[2]));  // open: I
  data_register_1 data_register_1_4 (.D(D[3]), .L(L), .CLK(CLK), .E(1'b1), .RE(RE), .Q(I[3]));  // open: I
  data_register_1 data_register_1_5 (.D(D[4]), .L(L), .CLK(CLK), .E(1'b1), .RE(RE), .Q(I[4]));  // open: I
  data_register_1 data_register_1_6 (.D(D[5]), .L(L), .CLK(CLK), .E(1'b1), .RE(RE), .Q(I[5]));  // open: I
  data_register_1 data_register_1_7 (.D(D[6]), .L(L), .CLK(CLK), .E(1'b1), .RE(RE), .Q(I[6]));  // open: I
  data_register_1 data_register_1_8 (.D(D[7]), .L(L), .CLK(CLK), .E(1'b1), .RE(RE), .Q(I[7]));  // open: I
  assign Q = E ? I : 8'bz;  // Controlled_Buffer controlled_buffer_1
endmodule

module ram_8_16 (
  input  E,
  input  L,
  input  CLK,
  input  [7:0] D,
  input  [3:0] A,
  output [7:0] Q
);

  wire [7:0] enabler_8_1_q, enabler_8_2_q, enabler_8_3_q, enabler_8_4_q;
  wire [15:0] decoder_16_1_q;

  decoder_16 decoder_16_1 (.I(A), .Q(decoder_16_1_q));
  enabler_8 enabler_8_1 (.D(decoder_16_1_q[7:0]), .E(E), .Q(enabler_8_1_q));
  enabler_8 enabler_8_2 (.D(decoder_16_1_q[15:8]), .E(E), .Q(enabler_8_2_q));
  enabler_8 enabler_8_3 (.D(decoder_16_1_q[7:0]), .E(L), .Q(enabler_8_3_q));
  enabler_8 enabler_8_4 (.D(decoder_16_1_q[15:8]), .E(L), .Q(enabler_8_4_q));
  data_register_8 data_register_8_1 (
    .D(D), .L(enabler_8_3_q[0]), .E(enabler_8_1_q[0]), .CLK(CLK), .RE(1'b0), .Q(Q));  // open: I
  data_register_8 data_register_8_2 (
    .D(D), .L(enabler_8_3_q[1]), .E(enabler_8_1_q[1]), .CLK(CLK), .RE(1'b0), .Q(Q));  // open: I
  data_register_8 data_register_8_3 (
    .D(D), .L(enabler_8_3_q[2]), .E(enabler_8_1_q[2]), .CLK(CLK), .RE(1'b0), .Q(Q));  // open: I
  data_register_8 data_register_8_4 (
    .D(D), .L(enabler_8_3_q[3]), .E(enabler_8_1_q[3]), .CLK(CLK), .RE(1'b0), .Q(Q));  // open: I
  data_register_8 data_register_8_5 (
    .D(D), .L(enabler_8_3_q[4]), .E(enabler_8_1_q[4]), .CLK(CLK), .RE(1'b0), .Q(Q));  // open: I
  data_register_8 data_register_8_6 (
    .D(D), .L(enabler_8_3_q[5]), .E(enabler_8_1_q[5]), .CLK(CLK), .RE(1'b0), .Q(Q));  // open: I
  data_register_8 data_register_8_7 (
    .D(D), .L(enabler_8_3_q[6]), .E(enabler_8_1_q[6]), .CLK(CLK), .RE(1'b0), .Q(Q));  // open: I
  data_register_8 data_register_8_8 (
    .D(D), .L(enabler_8_3_q[7]), .E(enabler_8_1_q[7]), .CLK(CLK), .RE(1'b0), .Q(Q));  // open: I
  data_register_8 data_register_8_9 (
    .D(D), .L(enabler_8_4_q[0]), .E(enabler_8_2_q[0]), .CLK(CLK), .RE(1'b0), .Q(Q));  // open: I
  data_register_8 data_register_8_10 (
    .D(D), .L(enabler_8_4_q[1]), .E(enabler_8_2_q[1]), .CLK(CLK), .RE(1'b0), .Q(Q));  // open: I
  data_register_8 data_register_8_11 (
    .D(D), .L(enabler_8_4_q[2]), .E(enabler_8_2_q[2]), .CLK(CLK), .RE(1'b0), .Q(Q));  // open: I
  data_register_8 data_register_8_12 (
    .D(D), .L(enabler_8_4_q[3]), .E(enabler_8_2_q[3]), .CLK(CLK), .RE(1'b0), .Q(Q));  // open: I
  data_register_8 data_register_8_13 (
    .D(D), .L(enabler_8_4_q[4]), .E(enabler_8_2_q[4]), .CLK(CLK), .RE(1'b0), .Q(Q));  // open: I
  data_register_8 data_register_8_14 (
    .D(D), .L(enabler_8_4_q[5]), .E(enabler_8_2_q[5]), .CLK(CLK), .RE(1'b0), .Q(Q));  // open: I
  data_register_8 data_register_8_15 (
    .D(D), .L(enabler_8_4_q[6]), .E(enabler_8_2_q[6]), .CLK(CLK), .RE(1'b0), .Q(Q));  // open: I
  data_register_8 data_register_8_16 (
    .D(D), .L(enabler_8_4_q[7]), .E(enabler_8_2_q[7]), .CLK(CLK), .RE(1'b0), .Q(Q));  // open: I
endmodule

module jk_latch (
  input  RE,
  input  J,
  input  K,
  input  E,
  output Q,
  output NQ
);

  wire and_1_out, and_2_out, and_3_out, and_4_out, not_1_out, or_1_out, or_2_out, sr_latch_1_nq, sr_latch_1_q;

  and and_1 (and_1_out, NQ, J, E);
  and and_2 (and_2_out, E, K, Q);
  or or_1 (or_1_out, RE, and_2_out);
  not not_1 (not_1_out, E);
  sr_latch sr_latch_1 (.R(and_1_out), .S(or_1_out), .Q(sr_latch_1_q), .NQ(sr_latch_1_nq));
  and and_3 (and_3_out, sr_latch_1_q, not_1_out);
  and and_4 (and_4_out, not_1_out, sr_latch_1_nq);
  or or_2 (or_2_out, RE, and_3_out);
  sr_latch sr_latch_2 (.R(or_2_out), .S(and_4_out), .Q(Q), .NQ(NQ));
endmodule

module counter_binary_4 (
  input  RE,
  input  C,
  output [3:0] Q,
  output RI
);

  wire not_1_out;

  not not_1 (not_1_out, C);
  jk_latch jk_latch_1 (.RE(RE), .J(1'b1), .K(1'b1), .E(not_1_out), .Q(Q[0]));  // open: NQ
  jk_latch jk_latch_2 (.RE(RE), .J(1'b1), .K(1'b1), .E(Q[0]), .Q(Q[1]));  // open: NQ
  jk_latch jk_latch_3 (.RE(RE), .J(1'b1), .K(1'b1), .E(Q[1]), .Q(Q[2]));  // open: NQ
  jk_latch jk_latch_4 (.RE(RE), .J(1'b1), .K(1'b1), .E(Q[2]), .Q(Q[3]));  // open: NQ

  assign RI = Q[3];
endmodule

module program_counter_4 (
  input  RE,
  input  C,
  input  CLK,
  input  J,
  input  [3:0] D,
  output [3:0] Q
);

  wire and_1_out, and_2_out, and_3_out, not_2_out, or_1_out, or_2_out;
  wire [3:0] not_1_out;

  assign not_1_out = ~D;  // NOT_Gate not_1, 4 bits wide
  and and_1 (and_1_out, C, CLK);
  not not_2 (not_2_out, and_1_out);
  and and_2 (and_2_out, J, CLK, D[0]);
  and and_3 (and_3_out, J, CLK, not_1_out[0]);
  or or_1 (or_1_out, C, and_2_out);
  or or_2 (or_2_out, C, and_3_out);
  jk_latch jk_latch_1 (.RE(RE), .J(or_1_out), .K(or_2_out), .E(not_2_out), .Q(Q[0]));  // open: NQ
  jk_latch jk_latch_2 (.RE(RE), .E(Q[0]), .Q(Q[1]));  // open: J, K, NQ
  jk_latch jk_latch_3 (.RE(RE), .E(Q[1]), .Q(Q[2]));  // open: J, K, NQ
  jk_latch jk_latch_4 (.RE(RE), .E(Q[2]), .Q(Q[3]));  // open: J, K, NQ
endmodule

module main (
  input  RE,
  input  PB,
  input  MODE_P0_R1,
  input  HT,
  input  MI,
  input  AI,
  input  AO,
  input  RO,
  input  RI,
  input  EO,
  input  SU,
  input  BI,
  input  BO,
  input  II,
  input  IO
);

  wire and_1_out, button_1_out, CLK_out, MAR_p6, not_1_out, or_1_out, or_2_out;
  wire [3:0] dipswitch_2_sw4, IR_i, IR_i_2, MAR_p1, MAR_p8, multiplexer_2_4_1_q, RAM_q;
  wire [7:0] A_i, ALU_i, B_i, dipswitch_1_sw8, dipswitch_3_sw8, IR_q, mulitplexer_2_8_1_q;

  Button button_1 (.out(button_1_out));
  or or_1 (or_1_out, RI, button_1_out);
  or or_2 (or_2_out, button_1_out, and_1_out);
  DipSwitch dipswitch_1 (
    .sw1(dipswitch_1_sw8[7]), .sw2(dipswitch_1_sw8[6]), .sw3(dipswitch_1_sw8[5]), .sw4(dipswitch_1_sw8[4]),
    .sw5(dipswitch_1_sw8[3]), .sw6(dipswitch_1_sw8[2]), .sw7(dipswitch_1_sw8[1]), .sw8(dipswitch_1_sw8[0]));
  DipSwitch #(.number(4)) dipswitch_2 (
    .sw1(dipswitch_2_sw4[3]), .sw2(dipswitch_2_sw4[2]), .sw3(dipswitch_2_sw4[1]), .sw4(dipswitch_2_sw4[0]));
  Clock CLK (.out(CLK_out));
  LedBar #(.matrixcols(4)) ledbar_1 (.led0(IR_i_2[3]), .led1(IR_i_2[2]), .led2(IR_i_2[1]), .led3(IR_i_2[0]));
  DipSwitch dipswitch_3 (
    .sw1(dipswitch_3_sw8[7]), .sw2(dipswitch_3_sw8[6]), .sw3(dipswitch_3_sw8[5]), .sw4(dipswitch_3_sw8[4]),
    .sw5(dipswitch_3_sw8[3]), .sw6(dipswitch_3_sw8[2]), .sw7(dipswitch_3_sw8[1]), .sw8(dipswitch_3_sw8[0]));
  not not_1 (not_1_out, HT);
  LedBar #(.matrixcols(4)) ledbar_2 (
    .led0(multiplexer_2_4_1_q[3]), .led1(multiplexer_2_4_1_q[2]), .led2(multiplexer_2_4_1_q[1]),
    .led3(multiplexer_2_4_1_q[0]));
  LedBar #(.matrixcols(4)) ledbar_3 (.led0(IR_i[3]), .led1(IR_i[2]), .led2(IR_i[1]), .led3(IR_i[0]));
  and and_1 (and_1_out, CLK_out, not_1_out);
  multiplexer_2_4 multiplexer_2_4_1 (.S(MODE_P0_R1), .A(dipswitch_2_sw4), .B(MAR_p8), .Q(multiplexer_2_4_1_q));
  // data_register_4 MAR: pin names not known; wires that end beside it: MAR_p1, MI, 1'b1, and_1_out, RE, MAR_p6, MAR_p6, MAR_p8
  ram_8_16 RAM (
    .E(RO), .L(or_1_out), .CLK(or_2_out), .D(mulitplexer_2_8_1_q), .A(multiplexer_2_4_1_q),
    .Q({RAM_q, MAR_p1}));
  mulitplexer_2_8 mulitplexer_2_8_1 (.S(MODE_P0_R1), .A(dipswitch_1_sw8), .B({RAM_q, MAR_p1}), .Q(mulitplexer_2_8_1_q));
  data_register_8 IR (.D({RAM_q, MAR_p1}), .L(II), .E(IO), .CLK(and_1_out), .RE(RE), .Q(IR_q), .I({IR_i_2, IR_i}));
  assign {RAM_q, MAR_p1} = PB ? dipswitch_3_sw8 : 8'bz;  // Controlled_Buffer controlled_buffer_1
  assign {RAM_q, MAR_p1} = IO ? {4'b0000, IR_q[3:0]} : 8'bz;  // Controlled_Buffer controlled_buffer_2
  LedBar ledbar_4 (
    .led0(RAM_q[3]), .led1(RAM_q[2]), .led2(RAM_q[1]), .led3(RAM_q[0]), .led4(MAR_p1[3]), .led5(MAR_p1[2]),
    .led6(MAR_p1[1]), .led7(MAR_p1[0]));
  LedBar ledbar_5 (
    .led0(A_i[7]), .led1(A_i[6]), .led2(A_i[5]), .led3(A_i[4]), .led4(A_i[3]), .led5(A_i[2]), .led6(A_i[1]),
    .led7(A_i[0]));
  LedBar ledbar_6 (
    .led0(ALU_i[7]), .led1(ALU_i[6]), .led2(ALU_i[5]), .led3(ALU_i[4]), .led4(ALU_i[3]), .led5(ALU_i[2]),
    .led6(ALU_i[1]), .led7(ALU_i[0]));
  LedBar ledbar_7 (
    .led0(B_i[7]), .led1(B_i[6]), .led2(B_i[5]), .led3(B_i[4]), .led4(B_i[3]), .led5(B_i[2]), .led6(B_i[1]),
    .led7(B_i[0]));
  data_register_8 A (.D({RAM_q, MAR_p1}), .L(AI), .E(AO), .CLK(and_1_out), .RE(RE), .Q({RAM_q, MAR_p1}), .I(A_i));
  arithmetic_unit_8 ALU (.CI(1'b0), .A(A_i), .B(B_i), .E(EO), .SU(SU), .S({RAM_q, MAR_p1}), .I(ALU_i));  // open: CO
  data_register_8 B (.D({RAM_q, MAR_p1}), .L(BI), .E(BO), .CLK(and_1_out), .RE(RE), .Q({RAM_q, MAR_p1}), .I(B_i));

  // Notes on the sheet:
  //   BUS
endmodule
