// Logisim project gates.circ as structural Verilog: 1 circuit, main circuit main
module main (
);

  wire and_1_out, and_2_out, buffer_1_out, controlled_buffer_1_out, controlled_inverter_1_out, nand_1_out,
       nand_2_out, nand_3_out, nand_4_out, nor_1_out, not_1_out, or_1_out, or_2_out, or_3_out,
       pull_resistor_2_node, pull_resistor_4_node, pull_resistor_6_node, transistor_1_out, transistor_3_out,
       transistor_4_out, transistor_6_out, transistor_7_out, transistor_11_out, transistor_12_out,
       transistor_14_out, transistor_15_out, transistor_16_out, transistor_18_out, xnor_1_out, xor_1_out;

  Transistor #(.\type ("n")) transistor_1 (.in(1'b1), .out(transistor_1_out), .gate(1'b0));
  Pull_Resistor pull_resistor_1 (.node(transistor_1_out));
  buf buffer_1 (buffer_1_out, 1'b0);
  Pull_Resistor #(.pull(1)) pull_resistor_2 (.node(pull_resistor_2_node));
  Transistor #(.\type ("n")) transistor_2 (.in(1'b0), .out(pull_resistor_2_node), .gate(1'b0));
  LED led_1 (.in(transistor_1_out));
  LED led_2 (.in(buffer_1_out));
  LED led_3 (.in(pull_resistor_2_node));
  not not_1 (not_1_out, 1'b0);
  LED led_4 (.in(not_1_out));
  Transistor #(.\type ("n")) transistor_3 (.in(1'b1), .out(transistor_3_out), .gate(1'b0));
  Transistor #(.\type ("n")) transistor_4 (.in(transistor_3_out), .out(transistor_4_out), .gate(1'b0));
  Pull_Resistor pull_resistor_3 (.node(transistor_4_out));
  and and_1 (and_1_out, 1'b0, 1'b0);
  Pull_Resistor #(.pull(1)) pull_resistor_4 (.node(pull_resistor_4_node));
  Transistor #(.\type ("n")) transistor_5 (.in(transistor_6_out), .out(pull_resistor_4_node), .gate(1'b0));
  Transistor #(.\type ("n")) transistor_6 (.in(1'b0), .out(transistor_6_out), .gate(1'b0));
  nand nand_1 (nand_1_out, 1'b0, 1'b0);
  LED led_5 (.in(transistor_4_out));
  LED led_6 (.in(and_1_out));
  LED led_7 (.in(pull_resistor_4_node));
  LED led_8 (.in(nand_1_out));
  Transistor #(.\type ("n")) transistor_7 (.in(1'b1), .out(transistor_7_out), .gate(1'b0));
  Pull_Resistor pull_resistor_5 (.node(transistor_7_out));
  Pull_Resistor #(.pull(1)) pull_resistor_6 (.node(pull_resistor_6_node));
  Transistor #(.\type ("n")) transistor_8 (.in(1'b0), .out(pull_resistor_6_node), .gate(1'b0));
  Transistor #(.\type ("n")) transistor_9 (.in(1'b1), .out(transistor_7_out), .gate(1'b0));
  LED led_9 (.in(transistor_7_out));
  or or_1 (or_1_out, 1'b0, 1'b0);
  LED led_10 (.in(or_1_out));
  Transistor #(.\type ("n")) transistor_10 (.in(1'b0), .out(pull_resistor_6_node), .gate(1'b0));
  LED led_11 (.in(pull_resistor_6_node));
  nor nor_1 (nor_1_out, 1'b0, 1'b0);
  LED led_12 (.in(nor_1_out));
  or or_2 (or_2_out, 1'b0, 1'b0);
  nand nand_2 (nand_2_out, 1'b0, 1'b0);
  xor xor_1 (xor_1_out, 1'b0, 1'b0);
  or or_3 (or_3_out, 1'b0, 1'b0);
  nand nand_3 (nand_3_out, 1'b0, 1'b0);
  xnor xnor_1 (xnor_1_out, 1'b0, 1'b0);
  and and_2 (and_2_out, or_2_out, nand_2_out);
  LED led_13 (.in(and_2_out));
  LED led_14 (.in(xor_1_out));
  LED led_15 (.in(nand_4_out));
  nand nand_4 (nand_4_out, or_3_out, nand_3_out);
  LED led_16 (.in(xnor_1_out));
  Transistor #(.\type ("n")) transistor_11 (.in(1'b1), .out(transistor_11_out), .gate(1'b0));
  Transistor #(.\type ("n")) transistor_12 (.in(transistor_11_out), .out(transistor_12_out), .gate(1'b0));
  LED led_17 (.in(transistor_12_out));
  Transistor transistor_13 (.in(transistor_14_out), .out(transistor_12_out), .gate(1'b0));
  Transistor #(.\type ("n")) transistor_14 (.in(1'b0), .out(transistor_14_out), .gate(1'b0));
  assign controlled_buffer_1_out = 1'b0 ? 1'b0 : 1'bz;  // Controlled_Buffer controlled_buffer_1
  LED led_18 (.in(controlled_buffer_1_out));
  Transistor #(.\type ("n")) transistor_15 (.in(1'b1), .out(transistor_15_out), .gate(1'b0));
  Transistor transistor_16 (.in(transistor_15_out), .out(transistor_16_out), .gate(1'b0));
  LED led_19 (.in(transistor_16_out));
  Transistor #(.\type ("n")) transistor_17 (.in(transistor_18_out), .out(transistor_16_out), .gate(1'b0));
  Transistor #(.\type ("n")) transistor_18 (.in(1'b0), .out(transistor_18_out), .gate(1'b0));
  assign controlled_inverter_1_out = 1'b0 ? ~1'b0 : 1'bz;  // Controlled_Inverter controlled_inverter_1
  LED led_20 (.in(controlled_inverter_1_out));
endmodule
