// Logisim project registers.circ as structural Verilog: 6 circuits, main circuit main
module main (
  input  [7:0] D,
  input  L,
  input  E,
  input  CLK,
  output [7:0] out_5
);

  wire [7:0] register_bit_1_q;

  register_bit register_bit_1 (.D(D[0]), .E(L), .CLK(CLK), .Q(register_bit_1_q[0]));
  register_bit register_bit_2 (.D(D[1]), .E(L), .CLK(CLK), .Q(register_bit_1_q[1]));
  register_bit register_bit_3 (.D(D[2]), .E(L), .CLK(CLK), .Q(register_bit_1_q[2]));
  register_bit register_bit_4 (.D(D[3]), .E(L), .CLK(CLK), .Q(register_bit_1_q[3]));
  register_bit register_bit_5 (.D(D[4]), .E(L), .CLK(CLK), .Q(register_bit_1_q[4]));
  register_bit register_bit_6 (.D(D[5]), .E(L), .CLK(CLK), .Q(register_bit_1_q[5]));
  register_bit register_bit_7 (.D(D[6]), .E(L), .CLK(CLK), .Q(register_bit_1_q[6]));
  register_bit register_bit_8 (.D(D[7]), .E(L), .CLK(CLK), .Q(register_bit_1_q[7]));
  assign out_5 = E ? register_bit_1_q : 8'bz;  // Controlled_Buffer controlled_buffer_1
endmodule

module or_latch (
  input  S,
  output Q
);

  or or_1 (Q, S, Q);
endmodule

module sr_latch (
  input  R,
  input  S,
  output Q,
  output NQ
);

  nor nor_1 (Q, R, NQ);
  nor nor_2 (NQ, Q, S);
endmodule

module d_latch (
  input  D,
  input  E,
  output Q,
  output NQ
);

  wire and_1_out, and_2_out, not_1_out;

  not not_1 (not_1_out, D);
  and and_1 (and_1_out, not_1_out, E);
  and and_2 (and_2_out, E, D);
  sr_latch sr_latch_1 (.R(and_1_out), .S(and_2_out), .Q(Q), .NQ(NQ));
endmodule

module d_flip_flop (
  input  D,
  input  RCLK,
  output Q,
  output NQ
);

  D_Flip_Flop d_ff_1 (.D(D), .clk(RCLK), .Q(Q), .Qn(NQ));  // open: preset, reset
endmodule

module register_bit (
  input  D,
  input  E,
  input  CLK,
  output Q
);

  wire and_1_out, and_2_out, not_1_out, or_1_out;

  not not_1 (not_1_out, E);
  and and_1 (and_1_out, Q, not_1_out);
  and and_2 (and_2_out, D, E);
  or or_1 (or_1_out, and_1_out, and_2_out);
  d_flip_flop d_flip_flop_1 (.D(or_1_out), .RCLK(CLK), .Q(Q));  // open: NQ
endmodule
